// Logisim project lab21.circ as structural Verilog: 1 circuit, main circuit main
module main (
  input  X,
  input  Y,
  output out_3
);

  wire and_1_out, and_2_out, not_1_out, not_2_out;

  not not_1 (not_1_out, X);
  and and_1 (and_1_out, not_1_out, Y);
  not not_2 (not_2_out, Y);
  and and_2 (and_2_out, not_2_out, X);
  or or_1 (out_3, and_1_out, and_2_out);

  // Notes on the sheet:
  //   XOR Circuit built using Logisim
  //   Beginners Tutorial
endmodule
