// Logisim project lab22.circ as structural Verilog: 3 circuits, main circuit full adder
module full_adder (
  input  A,
  input  B,
  input  Cin,
  output S,
  output Cout
);

  wire and_1_out, and_2_out, xor_1_out;

  xor xor_1 (xor_1_out, A, B);
  and and_1 (and_1_out, xor_1_out, Cin);
  and and_2 (and_2_out, A, B);
  xor xor_2 (S, xor_1_out, Cin);
  or or_1 (Cout, and_1_out, and_2_out);
endmodule

module _8_bit_adder (
  input  A,
  input  B,
  input  Cin,
  input  A_2,
  input  B_2,
  input  A_3,
  input  B_3,
  input  A_4,
  input  B_4,
  input  A_5,
  input  B_5,
  input  A_6,
  input  B_6,
  input  A_7,
  input  B_7,
  input  A_8,
  input  B_8,
  output S,
  output S_2,
  output S_3,
  output S_4,
  output S_5,
  output S_6,
  output S_7,
  output S_8,
  output Cout
);

  wire and_1_out, and_2_out, and_3_out, and_4_out, and_5_out, and_6_out, and_7_out, and_8_out, and_9_out,
       and_10_out, and_11_out, and_12_out, and_13_out, and_14_out, and_15_out, and_16_out, or_1_out,
       or_2_out, or_3_out, or_4_out, or_5_out, or_6_out, or_7_out, xor_1_out, xor_2_out, xor_3_out,
       xor_4_out, xor_5_out, xor_6_out, xor_7_out, xor_8_out;

  xor xor_1 (xor_1_out, A, B);
  xor xor_2 (xor_2_out, A_2, B_2);
  xor xor_3 (xor_3_out, A_3, B_3);
  xor xor_4 (xor_4_out, A_4, B_4);
  xor xor_5 (xor_5_out, A_5, B_5);
  xor xor_6 (xor_6_out, A_6, B_6);
  xor xor_7 (xor_7_out, A_7, B_7);
  xor xor_8 (xor_8_out, A_8, B_8);
  and and_1 (and_1_out, xor_1_out, Cin);
  and and_2 (and_2_out, A, B);
  and and_3 (and_3_out, xor_2_out, or_1_out);
  and and_4 (and_4_out, A_2, B_2);
  and and_5 (and_5_out, xor_3_out, or_2_out);
  and and_6 (and_6_out, A_3, B_3);
  and and_7 (and_7_out, xor_4_out, or_3_out);
  and and_8 (and_8_out, A_4, B_4);
  and and_9 (and_9_out, xor_5_out, or_4_out);
  and and_10 (and_10_out, A_5, B_5);
  and and_11 (and_11_out, xor_6_out, or_5_out);
  and and_12 (and_12_out, A_6, B_6);
  and and_13 (and_13_out, xor_7_out, or_6_out);
  and and_14 (and_14_out, A_7, B_7);
  and and_15 (and_15_out, xor_8_out, or_7_out);
  and and_16 (and_16_out, A_8, B_8);
  xor xor_9 (S, xor_1_out, Cin);
  or or_1 (or_1_out, and_1_out, and_2_out);
  xor xor_10 (S_2, xor_2_out, or_1_out);
  or or_2 (or_2_out, and_3_out, and_4_out);
  xor xor_11 (S_3, xor_3_out, or_2_out);
  or or_3 (or_3_out, and_5_out, and_6_out);
  xor xor_12 (S_4, xor_4_out, or_3_out);
  or or_4 (or_4_out, and_7_out, and_8_out);
  xor xor_13 (S_5, xor_5_out, or_4_out);
  or or_5 (or_5_out, and_9_out, and_10_out);
  xor xor_14 (S_6, xor_6_out, or_5_out);
  or or_6 (or_6_out, and_11_out, and_12_out);
  xor xor_15 (S_7, xor_7_out, or_6_out);
  or or_7 (or_7_out, and_13_out, and_14_out);
  xor xor_16 (S_8, xor_8_out, or_7_out);
  or or_8 (Cout, and_15_out, and_16_out);
endmodule

module _8_bit_adder_subtractor (
  input  Subtract_ON,
  input  A,
  input  B,
  input  A_2,
  input  B_2,
  input  A_3,
  input  B_3,
  input  A_4,
  input  B_4,
  input  A_5,
  input  B_5,
  input  A_6,
  input  B_6,
  input  A_7,
  input  B_7,
  input  A_8,
  input  B_8,
  output S,
  output S_2,
  output S_3,
  output S_4,
  output S_5,
  output S_6,
  output S_7,
  output S_8,
  output Cout
);

  wire and_1_out, and_2_out, and_3_out, and_4_out, and_5_out, and_6_out, and_7_out, and_8_out, and_9_out,
       and_10_out, and_11_out, and_12_out, and_13_out, and_14_out, and_15_out, and_16_out, or_1_out,
       or_2_out, or_3_out, or_4_out, or_5_out, or_6_out, or_7_out, or_8_out, xor_1_out, xor_2_out, xor_3_out,
       xor_4_out, xor_5_out, xor_6_out, xor_7_out, xor_8_out, xor_9_out, xor_10_out, xor_11_out, xor_12_out,
       xor_13_out, xor_14_out, xor_15_out, xor_16_out, xor_17_out;

  xor xor_1 (xor_1_out, B, Subtract_ON);
  xor xor_2 (xor_2_out, 1'b0, Subtract_ON);
  xor xor_3 (xor_3_out, B_2, Subtract_ON);
  xor xor_4 (xor_4_out, B_3, Subtract_ON);
  xor xor_5 (xor_5_out, B_4, Subtract_ON);
  xor xor_6 (xor_6_out, B_5, Subtract_ON);
  xor xor_7 (xor_7_out, B_6, Subtract_ON);
  xor xor_8 (xor_8_out, B_7, Subtract_ON);
  xor xor_9 (xor_9_out, B_8, Subtract_ON);
  xor xor_10 (xor_10_out, A, xor_1_out);
  xor xor_11 (xor_11_out, A_2, xor_3_out);
  xor xor_12 (xor_12_out, A_3, xor_4_out);
  xor xor_13 (xor_13_out, A_4, xor_5_out);
  xor xor_14 (xor_14_out, A_5, xor_6_out);
  xor xor_15 (xor_15_out, A_6, xor_7_out);
  xor xor_16 (xor_16_out, A_7, xor_8_out);
  xor xor_17 (xor_17_out, A_8, xor_9_out);
  and and_1 (and_1_out, xor_10_out, xor_2_out);
  and and_2 (and_2_out, A, xor_1_out);
  and and_3 (and_3_out, xor_11_out, or_1_out);
  and and_4 (and_4_out, A_2, xor_3_out);
  and and_5 (and_5_out, xor_12_out, or_2_out);
  and and_6 (and_6_out, A_3, xor_4_out);
  and and_7 (and_7_out, xor_13_out, or_3_out);
  and and_8 (and_8_out, A_4, xor_5_out);
  and and_9 (and_9_out, xor_14_out, or_4_out);
  and and_10 (and_10_out, A_5, xor_6_out);
  and and_11 (and_11_out, xor_15_out, or_5_out);
  and and_12 (and_12_out, A_6, xor_7_out);
  and and_13 (and_13_out, xor_16_out, or_6_out);
  and and_14 (and_14_out, A_7, xor_8_out);
  and and_15 (and_15_out, xor_17_out, or_7_out);
  and and_16 (and_16_out, A_8, xor_9_out);
  xor xor_18 (S, xor_10_out, xor_2_out);
  or or_1 (or_1_out, and_1_out, and_2_out);
  xor xor_19 (S_2, xor_11_out, or_1_out);
  or or_2 (or_2_out, and_3_out, and_4_out);
  xor xor_20 (S_3, xor_12_out, or_2_out);
  or or_3 (or_3_out, and_5_out, and_6_out);
  xor xor_21 (S_4, xor_13_out, or_3_out);
  or or_4 (or_4_out, and_7_out, and_8_out);
  xor xor_22 (S_5, xor_14_out, or_4_out);
  or or_5 (or_5_out, and_9_out, and_10_out);
  xor xor_23 (S_6, xor_15_out, or_5_out);
  or or_6 (or_6_out, and_11_out, and_12_out);
  xor xor_24 (S_7, xor_16_out, or_6_out);
  or or_7 (or_7_out, and_13_out, and_14_out);
  xor xor_25 (S_8, xor_17_out, or_7_out);
  or or_8 (or_8_out, and_15_out, and_16_out);
  xor xor_26 (Cout, or_8_out, Subtract_ON);
endmodule
