// Logisim project lab23.circ as structural Verilog: 1 circuit, main circuit main
module main (
);

  wire _0_05_out, _0_10_out, _0_25_out, _1_out, and_6_out, comparator_1_gt, not_1_out, or_2_out,
       Product__1_out, Reset_out, xor_1_out;
  wire [7:0] adder_1_out, and_1_out, and_2_out, and_3_out, and_4_out, and_5_out, bit_extender_1_out,
       bit_extender_2_out, bit_extender_3_out, bit_extender_4_out, bit_extender_5_out, or_1_out,
       register_1_q, subtractor_1_out;

  Button _1 (.out(_1_out));
  Button _0_25 (.out(_0_25_out));
  Button _0_10 (.out(_0_10_out));
  Button _0_05 (.out(_0_05_out));
  Button Product__1 (.out(Product__1_out));
  Button Reset (.out(Reset_out));
  ExactlyOne xor_1 (.out(xor_1_out), .in0(_0_05_out), .in1(_0_10_out), .in2(_0_25_out), .in3(_1_out));
  assign bit_extender_1_out = {{7{_1_out}}, _1_out};  // Bit_Extender bit_extender_1
  assign bit_extender_2_out = {{7{_0_25_out}}, _0_25_out};  // Bit_Extender bit_extender_2
  assign bit_extender_3_out = {{7{_0_10_out}}, _0_10_out};  // Bit_Extender bit_extender_3
  assign bit_extender_4_out = {{7{_0_05_out}}, _0_05_out};  // Bit_Extender bit_extender_4
  assign bit_extender_5_out = {{7{Product__1_out}}, Product__1_out};  // Bit_Extender bit_extender_5
  assign and_1_out = bit_extender_1_out & 8'h14;  // AND_Gate and_1, 8 bits wide
  assign and_2_out = bit_extender_2_out & 8'h5;  // AND_Gate and_2, 8 bits wide
  assign and_3_out = bit_extender_3_out & 8'h2;  // AND_Gate and_3, 8 bits wide
  assign and_4_out = bit_extender_4_out & 8'h1;  // AND_Gate and_4, 8 bits wide
  assign and_5_out = bit_extender_5_out & 8'h14;  // AND_Gate and_5, 8 bits wide
  assign or_1_out = and_1_out | and_2_out | and_3_out | and_4_out;  // OR_Gate or_1, 8 bits wide
  or or_2 (or_2_out, Product__1_out, xor_1_out);
  Adder adder_1 (.a(or_1_out), .b(register_1_q), .out(adder_1_out));  // open: cin, cout
  Subtractor subtractor_1 (.a(adder_1_out), .b(and_5_out), .out(subtractor_1_out));  // open: bin, bout
  and and_6 (and_6_out, or_2_out, not_1_out);
  Register #(.trigger("falling")) register_1 (
    .D(subtractor_1_out), .Q(register_1_q), .clk(and_6_out), .clr(Reset_out));  // open: en
  Comparator comparator_1 (.a(register_1_q), .b(8'h63), .gt(comparator_1_gt));  // open: eq, lt
  not not_1 (not_1_out, comparator_1_gt);
  Hex_Digit_Display hex_digit_display_1 (.value(register_1_q[3:0]));  // open: dp
  Hex_Digit_Display hex_digit_display_2 (.value(register_1_q[7:4]));  // open: dp
endmodule
