// Logisim project lab24.circ as structural Verilog: 2 circuits, main circuit main
module main (
);

  wire _0_05_out, _0_10_out, _0_25_out, _1_out, and_9_out, and_10_out, comparator_1_lt, comparator_2_lt,
       Iced_Coffee__3_60_out, Inactivity_Timer_out_2, not_1_out, not_2_out, or_2_out, or_4_out,
       Pringles__2_25_out, Skittles__1_95_out, undriven, Water__1_out, xor_1_out, xor_2_out;
  wire [7:0] adder_1_out, and_1_out, and_2_out, and_3_out, and_4_out, and_5_out, and_6_out, and_7_out,
       and_8_out, bit_extender_1_out, bit_extender_2_out, bit_extender_3_out, bit_extender_4_out,
       bit_extender_5_out, bit_extender_6_out, bit_extender_7_out, bit_extender_8_out, or_1_out, or_3_out,
       register_1_q, subtractor_1_out;

  Button _1 (.out(_1_out));
  Button _0_25 (.out(_0_25_out));
  Button _0_10 (.out(_0_10_out));
  Button _0_05 (.out(_0_05_out));
  Button Water__1 (.out(Water__1_out));
  Button Skittles__1_95 (.out(Skittles__1_95_out));
  Button Pringles__2_25 (.out(Pringles__2_25_out));
  Button Iced_Coffee__3_60 (.out(Iced_Coffee__3_60_out));
  ExactlyOne xor_1 (.out(xor_1_out), .in0(_0_05_out), .in1(_0_10_out), .in2(_0_25_out), .in3(_1_out));
  ExactlyOne xor_2 (
    .out(xor_2_out), .in0(Iced_Coffee__3_60_out), .in1(Pringles__2_25_out), .in2(Skittles__1_95_out),
    .in3(Water__1_out));
  assign bit_extender_1_out = {{7{_1_out}}, _1_out};  // Bit_Extender bit_extender_1
  assign bit_extender_2_out = {{7{_0_25_out}}, _0_25_out};  // Bit_Extender bit_extender_2
  assign bit_extender_3_out = {{7{_0_10_out}}, _0_10_out};  // Bit_Extender bit_extender_3
  assign bit_extender_4_out = {{7{_0_05_out}}, _0_05_out};  // Bit_Extender bit_extender_4
  assign bit_extender_5_out = {{7{Water__1_out}}, Water__1_out};  // Bit_Extender bit_extender_5
  assign bit_extender_6_out = {{7{Skittles__1_95_out}}, Skittles__1_95_out};  // Bit_Extender bit_extender_6
  assign bit_extender_7_out = {{7{Pringles__2_25_out}}, Pringles__2_25_out};  // Bit_Extender bit_extender_7
  assign bit_extender_8_out = {{7{Iced_Coffee__3_60_out}}, Iced_Coffee__3_60_out};  // Bit_Extender bit_extender_8
  assign and_1_out = bit_extender_1_out & 8'h14;  // AND_Gate and_1, 8 bits wide
  assign and_2_out = bit_extender_2_out & 8'h5;  // AND_Gate and_2, 8 bits wide
  assign and_3_out = bit_extender_3_out & 8'h2;  // AND_Gate and_3, 8 bits wide
  assign and_4_out = bit_extender_4_out & 8'h1;  // AND_Gate and_4, 8 bits wide
  assign and_5_out = bit_extender_5_out & 8'h14;  // AND_Gate and_5, 8 bits wide
  assign and_6_out = bit_extender_6_out & 8'h27;  // AND_Gate and_6, 8 bits wide
  assign and_7_out = bit_extender_7_out & 8'h2d;  // AND_Gate and_7, 8 bits wide
  assign and_8_out = bit_extender_8_out & 8'h48;  // AND_Gate and_8, 8 bits wide
  assign or_1_out = and_1_out | and_2_out | and_3_out | and_4_out;  // OR_Gate or_1, 8 bits wide
  or or_2 (or_2_out, xor_1_out, xor_2_out);
  Adder adder_1 (.a(or_1_out), .b(register_1_q), .out(adder_1_out));  // open: cin, cout
  assign or_3_out = and_5_out | and_6_out | and_7_out | and_8_out;  // OR_Gate or_3, 8 bits wide
  Subtractor subtractor_1 (.a(adder_1_out), .b(or_3_out), .out(subtractor_1_out));  // open: bin, bout
  and and_9 (and_9_out, or_2_out, not_1_out);
  Timer Inactivity_Timer (.in_1(or_2_out), .out_2(Inactivity_Timer_out_2));
  Register #(.trigger("falling")) register_1 (
    .D(subtractor_1_out), .en(and_10_out), .Q(register_1_q), .clk(and_9_out), .clr(Inactivity_Timer_out_2));
  and and_10 (and_10_out, not_1_out, comparator_2_lt);
  not not_1 (not_1_out, comparator_1_lt);
  Comparator comparator_1 (.a(register_1_q), .b(or_3_out), .lt(comparator_1_lt));  // open: gt, eq
  not not_2 (not_2_out, comparator_2_lt);
  Comparator comparator_2 (.a(subtractor_1_out), .b(8'h65), .lt(comparator_2_lt));  // open: gt, eq
  Hex_Digit_Display hex_digit_display_1 (.value(register_1_q[7:4]));  // open: dp
  Hex_Digit_Display hex_digit_display_2 (.value(register_1_q[3:0]));  // open: dp
  or or_4 (or_4_out, undriven, not_2_out, comparator_1_lt);
  LED LED_Error (.in(or_4_out));
endmodule

module Timer (
  input  in_1,
  output out_2
);

  wire clock_1_out;
  wire [7:0] counter_1_q;

  Clock clock_1 (.out(clock_1_out));
  Counter #(.max('h5)) counter_1 (.Q(counter_1_q), .clk(clock_1_out), .clr(in_1));  // open: load, D, count, carry
  Comparator comparator_1 (.a(counter_1_q), .b(8'h5), .eq(out_2));  // open: gt, lt
endmodule
